// Logisim project 8_Bit_ALU.circ as structural Verilog: 1 circuit, main circuit 8_Bit_ALU
module _8_Bit_ALU (
  input  Shift_Left,
  input  Shift_Right,
  input  Invert_Output,
  input  Carry_In,
  input  Inhibit_And,
  input  Inhibit_Carry,
  input  Invert_B,
  input  Invert_A,
  input  A128,
  input  B128,
  input  A64,
  input  B64,
  input  A32,
  input  B32,
  input  A16,
  input  B16,
  input  A8,
  input  B8,
  input  A4,
  input  B4,
  input  A2,
  input  B2,
  input  A1,
  input  B1,
  output _128,
  output _64,
  output _32,
  output _16,
  output _8,
  output _4,
  output _2,
  output _1,
  output Zero,
  output Half_Carry,
  output Carry_Overflow,
  output A_B,
  output A_B_2
);

  wire and_1_out, and_2_out, and_3_out, and_4_out, and_5_out, and_6_out, and_7_out, and_8_out, and_9_out,
       and_10_out, and_11_out, and_12_out, and_13_out, and_14_out, and_15_out, and_16_out, and_17_out,
       and_18_out, and_19_out, and_20_out, and_21_out, and_22_out, and_23_out, and_24_out, and_25_out,
       and_26_out, and_27_out, and_28_out, and_29_out, and_30_out, and_31_out, and_32_out, and_33_out,
       and_34_out, and_35_out, and_36_out, and_37_out, and_38_out, and_39_out, and_40_out, and_41_out,
       and_42_out, and_43_out, and_44_out, and_45_out, and_46_out, and_47_out, and_48_out, and_49_out,
       and_50_out, and_51_out, and_52_out, and_53_out, and_54_out, and_55_out, and_56_out, and_57_out,
       and_58_out, and_59_out, and_60_out, and_61_out, and_62_out, and_63_out, and_64_out, and_65_out,
       and_66_out, and_67_out, and_68_out, and_69_out, and_70_out, and_71_out, and_72_out, and_73_out,
       and_74_out, and_75_out, and_76_out, and_78_out, and_79_out, and_80_out, and_81_out, and_82_out,
       and_83_out, and_84_out, and_85_out, and_86_out, and_87_out, and_88_out, and_89_out, and_90_out,
       and_91_out, and_92_out, and_93_out, and_94_out, and_95_out, and_96_out, and_97_out, and_98_out,
       and_99_out, and_100_out, and_101_out, and_102_out, and_103_out, and_104_out, and_105_out, and_106_out,
       and_107_out, and_108_out, and_109_out, and_110_out, and_111_out, and_112_out, and_113_out,
       and_114_out, and_115_out, and_116_out, and_117_out, and_118_out, and_119_out, and_120_out,
       and_121_out, and_122_out, and_123_out, and_124_out, and_125_out, and_126_out, and_127_out,
       and_128_out, and_129_out, and_130_out, and_131_out, and_132_out, and_133_out, and_134_out,
       and_135_out, and_136_out, and_138_out, and_139_out, and_140_out, and_141_out, and_142_out, not_2_out,
       not_3_out, not_4_out, or_2_out, or_3_out, or_4_out, or_5_out, or_6_out, or_7_out, or_9_out, or_10_out,
       or_11_out, or_12_out, or_13_out, or_14_out, or_15_out, or_17_out, or_18_out, or_19_out, or_20_out,
       or_21_out, or_22_out, or_23_out, or_24_out, or_25_out, or_26_out, or_28_out, or_29_out, or_30_out,
       or_31_out, or_32_out, or_34_out, or_35_out, or_36_out, or_37_out, or_38_out, or_39_out, or_40_out,
       or_41_out, or_42_out, or_43_out, or_44_out, or_45_out, or_47_out, or_48_out, or_49_out, or_50_out,
       or_51_out, or_52_out, or_53_out, or_54_out, or_55_out, or_56_out, or_58_out, or_59_out, or_60_out,
       or_61_out, or_62_out, or_63_out, or_64_out, or_66_out, or_67_out, or_68_out, or_69_out, or_70_out,
       or_71_out, or_72_out, or_73_out, or_74_out, or_76_out, or_78_out, or_79_out;

  and and_1 (and_1_out, Shift_Left, and_8_out);
  not not_1 (Zero, or_9_out);
  and and_2 (and_2_out, ~and_10_out, or_3_out);  // AND_Gate
  and and_3 (and_3_out, ~Inhibit_Carry, or_4_out);  // AND_Gate
  or or_1 (Carry_Overflow, and_1_out, and_3_out);
  and and_4 (and_4_out, Invert_A, A128);
  and and_5 (and_5_out, ~and_17_out, or_7_out);  // AND_Gate
  and and_6 (and_6_out, and_8_out, Shift_Right);
  and and_7 (and_7_out, not_4_out, not_3_out, and_8_out);
  and and_8 (and_8_out, or_2_out, ~and_9_out);  // AND_Gate
  and and_9 (and_9_out, Invert_Output, and_2_out);
  or or_2 (or_2_out, Invert_Output, and_2_out);
  or or_3 (or_3_out, and_11_out, and_22_out);
  and and_10 (and_10_out, and_11_out, and_22_out);
  and and_11 (and_11_out, ~and_12_out, or_5_out);  // AND_Gate
  or or_4 (or_4_out, and_10_out, and_12_out);
  and and_12 (and_12_out, and_14_out, ~Inhibit_And, and_13_out);  // AND_Gate
  or or_5 (or_5_out, and_14_out, and_13_out);
  and and_13 (and_13_out, ~and_15_out, or_13_out);  // AND_Gate
  and and_14 (and_14_out, ~and_4_out, or_6_out);  // AND_Gate
  or or_6 (or_6_out, A128, Invert_A);
  and and_15 (and_15_out, Invert_B, B128);
  and and_16 (and_16_out, A128, and_5_out);
  not not_2 (not_2_out, and_5_out);
  and and_17 (and_17_out, A128, B128);
  or or_7 (or_7_out, A128, B128);
  or or_8 (_128, and_7_out, and_19_out);
  and and_18 (and_18_out, not_4_out, not_3_out, and_29_out);
  and and_19 (and_19_out, Shift_Left, and_29_out);
  or or_9 (or_9_out, or_17_out, and_8_out);
  or or_10 (or_10_out, Invert_Output, and_20_out);
  and and_20 (and_20_out, ~and_21_out, or_11_out);  // AND_Gate
  or or_11 (or_11_out, and_32_out, and_41_out);
  and and_21 (and_21_out, and_32_out, and_41_out);
  or or_12 (or_12_out, and_21_out, and_33_out);
  and and_22 (and_22_out, ~Inhibit_Carry, or_12_out);  // AND_Gate
  and and_23 (and_23_out, ~and_24_out, or_14_out);  // AND_Gate
  or or_13 (or_13_out, B128, Invert_B);
  or or_14 (or_14_out, A64, Invert_A);
  and and_24 (and_24_out, Invert_A, A64);
  and and_25 (and_25_out, A64, not_2_out, and_26_out);
  and and_26 (and_26_out, ~and_36_out, or_15_out);  // AND_Gate
  and and_27 (and_27_out, ~and_26_out, not_2_out);  // AND_Gate
  or or_15 (or_15_out, A64, B64);
  or or_16 (_64, and_6_out, and_18_out, and_38_out);
  and and_28 (and_28_out, and_29_out, Shift_Right);
  or or_17 (or_17_out, or_28_out, and_29_out);
  and and_29 (and_29_out, or_10_out, ~and_30_out);  // AND_Gate
  and and_30 (and_30_out, Invert_Output, and_20_out);
  and and_31 (and_31_out, ~and_40_out, or_22_out);  // AND_Gate
  and and_32 (and_32_out, ~and_33_out, or_18_out);  // AND_Gate
  and and_33 (and_33_out, and_23_out, ~Inhibit_And, and_34_out);  // AND_Gate
  or or_18 (or_18_out, and_23_out, and_34_out);
  and and_34 (and_34_out, ~and_35_out, or_19_out);  // AND_Gate
  or or_19 (or_19_out, B64, Invert_B);
  and and_35 (and_35_out, Invert_B, B64);
  or or_20 (or_20_out, and_16_out, and_25_out);
  and and_36 (and_36_out, A64, B64);
  and and_37 (and_37_out, not_4_out, not_3_out, and_52_out);
  and and_38 (and_38_out, Shift_Left, and_52_out);
  or or_21 (or_21_out, Invert_Output, and_31_out);
  and and_39 (and_39_out, Invert_Output, and_31_out);
  or or_22 (or_22_out, and_55_out, and_56_out);
  and and_40 (and_40_out, and_55_out, and_56_out);
  and and_41 (and_41_out, ~Inhibit_Carry, or_23_out);  // AND_Gate
  and and_42 (and_42_out, and_43_out, ~Inhibit_And, and_57_out);  // AND_Gate
  or or_23 (or_23_out, and_40_out, and_42_out);
  and and_43 (and_43_out, ~and_44_out, or_24_out);  // AND_Gate
  or or_24 (or_24_out, A32, Invert_A);
  and and_44 (and_44_out, Invert_A, A32);
  and and_45 (and_45_out, Invert_B, B32);
  or or_25 (or_25_out, or_20_out, and_46_out);
  and and_46 (and_46_out, A32, and_27_out, and_47_out);
  and and_47 (and_47_out, ~and_49_out, or_26_out);  // AND_Gate
  and and_48 (and_48_out, ~and_47_out, and_27_out);  // AND_Gate
  and and_49 (and_49_out, A32, B32);
  or or_26 (or_26_out, A32, B32);
  or or_27 (_32, and_28_out, and_37_out, and_50_out);
  and and_50 (and_50_out, Shift_Left, and_64_out);
  and and_51 (and_51_out, and_52_out, Shift_Right);
  or or_28 (or_28_out, or_40_out, and_52_out);
  and and_52 (and_52_out, or_21_out, ~and_39_out);  // AND_Gate
  or or_29 (or_29_out, Invert_Output, and_53_out);
  and and_53 (and_53_out, ~and_54_out, or_30_out);  // AND_Gate
  or or_30 (or_30_out, and_66_out, Half_Carry);
  and and_54 (and_54_out, and_66_out, Half_Carry);
  and and_55 (and_55_out, ~and_42_out, or_31_out);  // AND_Gate
  or or_31 (or_31_out, and_43_out, and_57_out);
  and and_56 (and_56_out, ~Inhibit_Carry, or_34_out);  // AND_Gate
  and and_57 (and_57_out, ~and_45_out, or_32_out);  // AND_Gate
  or or_32 (or_32_out, B32, Invert_B);
  and and_58 (and_58_out, Invert_A, A16);
  and and_59 (and_59_out, A16, and_48_out, and_60_out);
  and and_60 (and_60_out, ~and_71_out, or_39_out);  // AND_Gate
  and and_61 (and_61_out, ~and_60_out, and_48_out);  // AND_Gate
  or or_33 (_16, and_51_out, and_62_out, and_73_out);
  and and_62 (and_62_out, not_4_out, not_3_out, and_64_out);
  and and_63 (and_63_out, and_64_out, Shift_Right);
  and and_64 (and_64_out, or_29_out, ~and_65_out);  // AND_Gate
  and and_65 (and_65_out, Invert_Output, and_53_out);
  and and_66 (and_66_out, ~and_67_out, or_35_out);  // AND_Gate
  or or_34 (or_34_out, and_54_out, and_67_out);
  and and_67 (and_67_out, and_69_out, ~Inhibit_And, and_68_out);  // AND_Gate
  or or_35 (or_35_out, and_69_out, and_68_out);
  and and_68 (and_68_out, ~and_70_out, or_37_out);  // AND_Gate
  and and_69 (and_69_out, ~and_58_out, or_36_out);  // AND_Gate
  or or_36 (or_36_out, A16, Invert_A);
  or or_37 (or_37_out, B16, Invert_B);
  and and_70 (and_70_out, Invert_B, B16);
  or or_38 (or_38_out, or_25_out, and_59_out);
  and and_71 (and_71_out, A16, B16);
  or or_39 (or_39_out, A16, B16);
  and and_72 (and_72_out, not_4_out, not_3_out, and_86_out);
  and and_73 (and_73_out, Shift_Left, and_86_out);
  or or_40 (or_40_out, or_47_out, and_64_out);
  or or_41 (or_41_out, Invert_Output, and_75_out);
  and and_74 (and_74_out, Invert_Output, and_75_out);
  and and_75 (and_75_out, ~and_76_out, or_42_out);  // AND_Gate
  or or_42 (or_42_out, and_88_out, and_97_out);
  and and_76 (and_76_out, and_88_out, and_97_out);
  or or_43 (or_43_out, and_76_out, and_78_out);
  and and_77 (Half_Carry, ~Inhibit_Carry, or_43_out);  // AND_Gate
  and and_78 (and_78_out, and_79_out, ~Inhibit_And, and_89_out);  // AND_Gate
  and and_79 (and_79_out, ~and_80_out, or_44_out);  // AND_Gate
  or or_44 (or_44_out, A8, Invert_A);
  and and_80 (and_80_out, Invert_A, A8);
  and and_81 (and_81_out, A8, and_61_out, and_82_out);
  and and_82 (and_82_out, ~and_91_out, or_45_out);  // AND_Gate
  and and_83 (and_83_out, ~and_82_out, and_61_out);  // AND_Gate
  or or_45 (or_45_out, A8, B8);
  or or_46 (_8, and_63_out, and_72_out, and_84_out);
  and and_84 (and_84_out, Shift_Left, and_93_out);
  and and_85 (and_85_out, and_86_out, Shift_Right);
  or or_47 (or_47_out, or_58_out, and_86_out);
  and and_86 (and_86_out, or_41_out, ~and_74_out);  // AND_Gate
  and and_87 (and_87_out, ~and_95_out, or_52_out);  // AND_Gate
  and and_88 (and_88_out, ~and_78_out, or_48_out);  // AND_Gate
  or or_48 (or_48_out, and_79_out, and_89_out);
  and and_89 (and_89_out, ~and_90_out, or_49_out);  // AND_Gate
  or or_49 (or_49_out, B8, Invert_B);
  and and_90 (and_90_out, Invert_B, B8);
  or or_50 (or_50_out, or_38_out, and_81_out);
  and and_91 (and_91_out, A8, B8);
  and and_92 (and_92_out, not_4_out, not_3_out, and_93_out);
  and and_93 (and_93_out, or_51_out, ~and_94_out);  // AND_Gate
  and and_94 (and_94_out, Invert_Output, and_87_out);
  or or_51 (or_51_out, Invert_Output, and_87_out);
  or or_52 (or_52_out, and_96_out, and_110_out);
  and and_95 (and_95_out, and_96_out, and_110_out);
  and and_96 (and_96_out, ~and_98_out, or_61_out);  // AND_Gate
  and and_97 (and_97_out, ~Inhibit_Carry, or_53_out);  // AND_Gate
  or or_53 (or_53_out, and_95_out, and_98_out);
  and and_98 (and_98_out, and_99_out, ~Inhibit_And, and_112_out);  // AND_Gate
  and and_99 (and_99_out, ~and_101_out, or_54_out);  // AND_Gate
  or or_54 (or_54_out, A4, Invert_A);
  and and_100 (and_100_out, Invert_B, B4);
  and and_101 (and_101_out, Invert_A, A4);
  or or_55 (or_55_out, or_50_out, and_102_out);
  and and_102 (and_102_out, A4, and_83_out, and_103_out);
  and and_103 (and_103_out, ~and_105_out, or_56_out);  // AND_Gate
  and and_104 (and_104_out, ~and_103_out, and_83_out);  // AND_Gate
  and and_105 (and_105_out, A4, B4);
  or or_56 (or_56_out, A4, B4);
  or or_57 (_4, and_85_out, and_92_out, and_106_out);
  and and_106 (and_106_out, Shift_Left, and_119_out);
  and and_107 (and_107_out, and_93_out, Shift_Right);
  or or_58 (or_58_out, or_66_out, and_93_out);
  or or_59 (or_59_out, Invert_Output, and_108_out);
  and and_108 (and_108_out, ~and_109_out, or_60_out);  // AND_Gate
  or or_60 (or_60_out, and_121_out, and_131_out);
  and and_109 (and_109_out, and_121_out, and_131_out);
  or or_61 (or_61_out, and_99_out, and_112_out);
  and and_110 (and_110_out, ~Inhibit_Carry, or_62_out);  // AND_Gate
  or or_62 (or_62_out, and_109_out, and_122_out);
  and and_111 (and_111_out, ~and_113_out, or_68_out);  // AND_Gate
  and and_112 (and_112_out, ~and_100_out, or_63_out);  // AND_Gate
  or or_63 (or_63_out, B4, Invert_B);
  and and_113 (and_113_out, Invert_A, A2);
  and and_114 (and_114_out, A2, and_104_out, and_115_out);
  and and_115 (and_115_out, ~and_125_out, or_64_out);  // AND_Gate
  and and_116 (and_116_out, ~and_115_out, and_104_out);  // AND_Gate
  or or_64 (or_64_out, A2, B2);
  or or_65 (_2, and_107_out, and_118_out, and_126_out);
  and and_117 (and_117_out, and_119_out, Shift_Right);
  and and_118 (and_118_out, not_4_out, not_3_out, and_119_out);
  or or_66 (or_66_out, and_139_out, and_119_out);
  and and_119 (and_119_out, or_59_out, ~and_120_out);  // AND_Gate
  and and_120 (and_120_out, Invert_Output, and_108_out);
  and and_121 (and_121_out, ~and_122_out, or_67_out);  // AND_Gate
  and and_122 (and_122_out, and_111_out, ~Inhibit_And, and_123_out);  // AND_Gate
  or or_67 (or_67_out, and_111_out, and_123_out);
  and and_123 (and_123_out, ~and_124_out, or_69_out);  // AND_Gate
  or or_68 (or_68_out, A2, Invert_A);
  or or_69 (or_69_out, B2, Invert_B);
  and and_124 (and_124_out, Invert_B, B2);
  or or_70 (or_70_out, or_55_out, and_114_out);
  and and_125 (and_125_out, A2, B2);
  and and_126 (and_126_out, Shift_Left, and_139_out);
  and and_127 (and_127_out, not_4_out, not_3_out, and_139_out);
  and and_128 (and_128_out, Invert_Output, and_129_out);
  or or_71 (or_71_out, Invert_Output, and_129_out);
  and and_129 (and_129_out, ~and_130_out, or_72_out);  // AND_Gate
  or or_72 (or_72_out, and_140_out, Carry_In);
  and and_130 (and_130_out, and_140_out, Carry_In);
  or or_73 (or_73_out, and_130_out, and_132_out);
  and and_131 (and_131_out, ~Inhibit_Carry, or_73_out);  // AND_Gate
  and and_132 (and_132_out, and_133_out, ~Inhibit_And, and_141_out);  // AND_Gate
  and and_133 (and_133_out, ~and_134_out, or_74_out);  // AND_Gate
  or or_74 (or_74_out, A1, Invert_A);
  and and_134 (and_134_out, Invert_A, A1);
  or or_75 (A_B, or_70_out, and_135_out);
  and and_135 (and_135_out, A1, and_116_out, and_136_out);
  and and_136 (and_136_out, ~and_138_out, or_76_out);  // AND_Gate
  and and_137 (A_B_2, ~and_136_out, and_116_out);  // AND_Gate
  and and_138 (and_138_out, A1, B1);
  or or_76 (or_76_out, A1, B1);
  or or_77 (_1, and_117_out, and_127_out);
  not not_3 (not_3_out, Shift_Left);
  not not_4 (not_4_out, Shift_Right);
  and and_139 (and_139_out, or_71_out, ~and_128_out);  // AND_Gate
  and and_140 (and_140_out, ~and_132_out, or_78_out);  // AND_Gate
  or or_78 (or_78_out, and_133_out, and_141_out);
  and and_141 (and_141_out, ~and_142_out, or_79_out);  // AND_Gate
  or or_79 (or_79_out, B1, Invert_B);
  and and_142 (and_142_out, Invert_B, B1);
endmodule
